// Logisim project 11.circ as structural Verilog
module nor_latch (
  input  S,
  input  R,
  output out_3,
  output Q
);

  wire not_1_out, not_2_out;

  not not_1 (not_1_out, not_2_out);
  nor nor_1 (out_3, Q, S);
  not not_2 (not_2_out, not_1_out);
  nor nor_2 (Q, out_3, R);

  // Notes on the sheet:
  //   P
endmodule

module s_r_latch (
  input  S,
  input  R,
  output Q_comp,
  output Q
);

  nor nor_1 (Q_comp, S, Q);
  nor nor_2 (Q, Q_comp, R);
endmodule

module s_r_latch_nand_inverter (
  input  S_comp,
  input  R_comp,
  output Q,
  output Q_comp
);

  nand nand_1 (Q, S_comp, Q_comp);
  nand nand_2 (Q_comp, Q, R_comp);
endmodule

module gated_s_r_latch (
  input  S,
  input  G,
  input  R,
  output Q,
  output Q_comp
);

  wire nand_1_out, nand_2_out;

  nand nand_1 (nand_1_out, S, G);
  nand nand_2 (nand_2_out, G, R);
  nand nand_3 (Q, nand_1_out, Q_comp);
  nand nand_4 (Q_comp, Q, nand_2_out);
endmodule

module gated_d_latch (
  input  D,
  input  G,
  output Q,
  output Q_comp
);

  wire and_1_out, and_2_out, not_1_out;

  not not_1 (not_1_out, D);
  and and_1 (and_1_out, D, G);
  and and_2 (and_2_out, G, not_1_out);
  s_r_latch s_r_latch_1 (.Q_comp(Q_comp), .Q(Q), .S(and_1_out), .R(and_2_out));
endmodule

module s_r_latch_nand (
  input  S,
  input  R,
  output Q,
  output Q_comp
);

  wire nand_1_out, nand_2_out;

  nand nand_1 (nand_1_out, S, S);
  nand nand_2 (nand_2_out, R, R);
  nand nand_3 (Q, nand_1_out, Q_comp);
  nand nand_4 (Q_comp, Q, nand_2_out);
endmodule

module d_flip_flop_rising_edge (
  input  D,
  output Q
);

  wire Ck_out;

  D_Flip_Flop d_ff_1 (.D(D), .clk(Ck_out), .Q(Q));  // open: Qn, preset, reset
  Clock Ck (.out(Ck_out));
endmodule

module d_flip_flop_gated_d_latch (
  input  D,
  output P,
  output Q,
  output G1,
  output G2
);

  Clock CLK (.out(G2));
  not not_1 (G1, G2);
  gated_d_latch gated_d_latch_1 (.Q(P), .G(G1), .D(D));  // open: Q_comp
  gated_d_latch gated_d_latch_2 (.Q(Q), .G(G2), .D(P));  // open: Q_comp
endmodule

module s_r_flip_flop_s_r_latch (
  input  S,
  input  R,
  output P,
  output Q,
  output Q_comp,
  output CLK_comp
);

  wire and_1_out, and_2_out, and_3_out, and_4_out, CLK_out, Master_q_comp;

  Clock CLK (.out(CLK_out));
  not not_1 (CLK_comp, CLK_out);
  and and_1 (and_1_out, S, CLK_comp);
  and and_2 (and_2_out, CLK_comp, R);
  s_r_latch Master (.Q_comp(Master_q_comp), .Q(P), .S(and_1_out), .R(and_2_out));
  and and_3 (and_3_out, CLK_out, P);
  and and_4 (and_4_out, Master_q_comp, CLK_out);
  s_r_latch Slave (.Q_comp(Q_comp), .Q(Q), .S(and_3_out), .R(and_4_out));
endmodule

module j_k_flip_flop (
  input  J,
  input  K,
  output Q
);

  wire CK_out;

  Clock CK (.out(CK_out));
  J_K_Flip_Flop j_k_ff_1 (.J(J), .K(K), .clk(CK_out), .Q(Q));  // open: Qn, preset, reset
endmodule

module j_k_flip_flop_s_r_latch (
  input  J,
  input  K,
  output P,
  output Q,
  output Q_comp,
  output CLK_comp
);

  wire and_1_out, and_2_out, and_3_out, and_4_out, CLK_out, Master_q_comp;

  Clock CLK (.out(CLK_out));
  not not_1 (CLK_comp, CLK_out);
  and and_1 (and_1_out, Q_comp, J, CLK_comp);
  and and_2 (and_2_out, CLK_comp, K, Q);
  s_r_latch Master (.Q_comp(Master_q_comp), .Q(P), .S(and_1_out), .R(and_2_out));
  and and_3 (and_3_out, CLK_out, P);
  and and_4 (and_4_out, Master_q_comp, CLK_out);
  s_r_latch Slave (.Q_comp(Q_comp), .Q(Q), .S(and_3_out), .R(and_4_out));
endmodule

module t_flip_flop (
  input  T,
  output Q
);

  wire Ck_out;

  Clock Ck (.out(Ck_out));
  T_Flip_Flop t_ff_1 (.T(T), .clk(Ck_out), .Q(Q));  // open: Qn, reset, preset
endmodule

module t_flip_flop_d_flip_flop (
  input  T,
  output Q,
  output Q_comp
);

  wire CLK_out, xor_1_out;

  Clock CLK (.out(CLK_out));
  D_Flip_Flop d_ff_1 (.D(xor_1_out), .clk(CLK_out), .Q(Q), .Qn(Q_comp));  // open: preset, reset
  xor xor_1 (xor_1_out, Q, T);
endmodule

module t_flip_flop_j_k_flip_flop (
  input  T,
  output Q,
  output Q_comp
);

  wire CK_out;

  J_K_Flip_Flop j_k_ff_1 (.J(T), .K(CK_out), .clk(T), .Q(Q), .Qn(Q_comp));  // open: preset, reset
  Clock CK (.out(CK_out));
endmodule
