// Logisim project 2.circ as structural Verilog
module s (
  input  in_1,
  output out_2
);

  // Switch switch_1: pin names not known; wires that end beside it: in_1, out_2
endmodule

module and_switch (
  input  in_1,
  output C
);

  wire A_p2;

  // Switch A: pin names not known; wires that end beside it: in_1, A_p2, A_p2
  // Switch B: pin names not known; wires that end beside it: C
endmodule

module or_switch (
  input  in_1,
  output out_2
);

  // Switch switch_1: pin names not known; wires that end beside it: in_1, out_2
  // Switch switch_2: pin names not known; wires that end beside it: in_1, out_2
endmodule
