// Logisim project 8.circ as structural Verilog
module three_input_nor_8_2 (
  input  a,
  input  b,
  input  c,
  input  d,
  output out_5
);

  wire nor_1_out, nor_2_out, nor_3_out, nor_4_out, nor_5_out, nor_6_out, nor_7_out, not_1_out, not_2_out,
       not_3_out, not_4_out;

  not not_1 (not_1_out, a);
  not not_2 (not_2_out, b);
  not not_3 (not_3_out, c);
  not not_4 (not_4_out, d);
  nor nor_1 (nor_1_out, not_1_out, not_2_out, c);
  nor nor_2 (nor_2_out, b, not_4_out);
  nor nor_3 (nor_3_out, a, c);
  nor nor_4 (nor_4_out, not_1_out, not_3_out);
  nor nor_5 (nor_5_out, a, not_3_out, nor_2_out);
  nor nor_6 (nor_6_out, nor_3_out, nor_4_out);
  nor nor_7 (nor_7_out, b, not_4_out, nor_6_out);
  nor nor_8 (out_5, nor_1_out, nor_5_out, nor_7_out);
endmodule

module gate_delays_8_3 (
  input  A,
  input  B,
  input  C,
  output G1,
  output G2
);

  and and_1 (G1, A, B);
  nor nor_1 (G2, G1, C);
endmodule

module hazard1_1_8_4 (
  input  A,
  input  B,
  input  C,
  output D,
  output F,
  output E
);

  wire not_1_out;

  not not_1 (not_1_out, B);
  and and_1 (D, A, not_1_out);
  and and_2 (E, B, C);
  or or_1 (F, D, E);
endmodule

module hazard2_8_4 (
  input  A,
  output F,
  output B
);

  not not_1 (B, A);
  and and_1 (F, A, B);
endmodule

module hazard1_2_8_4 (
  input  A,
  input  B,
  input  C,
  output D,
  output F,
  output E
);

  wire and_2_out, not_1_out;

  not not_1 (not_1_out, B);
  and and_1 (D, A, not_1_out);
  and and_2 (and_2_out, A, C);
  and and_3 (E, B, C);
  or or_1 (F, D, and_2_out, E);
endmodule

module seven_seg (
);

  _7_Segment_Display u_7_segment_display_1 ();  // open: g, f, a, b, e, d, c, dp

  // Notes on the sheet:
  //   1
  //   2
  //   3
  //   4
  //   3
  //   2
  //   4
  //   1
  //   5
  //   7
  //   6
  //   8
  //   5
  //   6
  //   7
  //   8
endmodule

module bcd_to_7seg (
  input  A,
  input  B,
  input  C,
  input  D,
  output F1,
  output F2,
  output F3,
  output F4,
  output F5,
  output F6,
  output F7
);

  wire nand_1_out, nand_2_out, nand_3_out, nand_4_out, nand_5_out, nand_6_out, nand_8_out, nand_12_out,
       nor_1_out, not_1_out, not_2_out, not_3_out, not_4_out, xor_1_out, xor_2_out;

  not not_1 (not_1_out, A);
  not not_2 (not_2_out, B);
  not not_3 (not_3_out, C);
  not not_4 (not_4_out, D);
  nand nand_1 (nand_1_out, B, not_3_out);
  nand nand_2 (nand_2_out, B, D);
  nand nand_3 (nand_3_out, not_3_out, not_4_out);
  xor xor_1 (xor_1_out, B, D);
  xor xor_2 (xor_2_out, C, D);
  nor nor_1 (nor_1_out, not_2_out, C);
  nand nand_4 (nand_4_out, D, not_3_out);
  nand nand_5 (nand_5_out, C, not_4_out);
  nand nand_6 (nand_6_out, B, not_3_out, D);
  nand nand_7 (F7, C, not_4_out, not_2_out);
  nand nand_8 (nand_8_out, C, nand_2_out);
  nand nand_9 (F2, not_2_out, not_1_out, nand_3_out);
  nand nand_10 (F3, not_1_out, not_3_out, xor_1_out);
  nand nand_11 (F4, not_1_out, B, xor_2_out);
  nor nor_2 (F5, D, nor_1_out);
  nand nand_12 (nand_12_out, not_2_out, nand_4_out);
  nand nand_13 (F1, not_1_out, nand_1_out, nand_8_out);
  nand nand_14 (F6, nand_12_out, nand_5_out, nand_6_out);
endmodule

module two_bit_multiplier (
  input  A1,
  input  A0,
  input  B1,
  input  B0,
  output C3,
  output C2,
  output C1,
  output C0
);

  wire nand_1_out, nand_2_out, nand_3_out, nand_4_out, nor_2_out, not_1_out, not_2_out, not_3_out, not_4_out;

  not not_1 (not_1_out, A1);
  not not_2 (not_2_out, A0);
  not not_3 (not_3_out, B1);
  not not_4 (not_4_out, B0);
  nor nor_1 (C3, not_1_out, not_2_out, not_3_out, not_4_out);
  nor nor_2 (nor_2_out, not_4_out, not_2_out);
  nand nand_1 (nand_1_out, B1, A0);
  nand nand_2 (nand_2_out, A1, B0);
  nor nor_3 (C0, not_2_out, not_4_out);
  nor nor_4 (C2, not_1_out, not_3_out, nor_2_out);
  nand nand_3 (nand_3_out, A1, B0, nand_1_out);
  nand nand_4 (nand_4_out, A0, B1, nand_2_out);
  nand nand_5 (C1, nand_3_out, nand_4_out);
endmodule

module hw4_2 (
  input  A1,
  input  A0,
  input  B1,
  input  B0,
  output C3,
  output C2,
  output C1,
  output C0
);

  wire bcd_to_7seg_1_f1, bcd_to_7seg_1_f2, bcd_to_7seg_1_f3, bcd_to_7seg_1_f4, bcd_to_7seg_1_f5,
       bcd_to_7seg_1_f6, bcd_to_7seg_1_f7, bcd_to_7seg_2_f1, bcd_to_7seg_2_f2, bcd_to_7seg_2_f3,
       bcd_to_7seg_2_f4, bcd_to_7seg_2_f5, bcd_to_7seg_2_f6, bcd_to_7seg_2_f7, bcd_to_7seg_3_f1,
       bcd_to_7seg_3_f2, bcd_to_7seg_3_f3, bcd_to_7seg_3_f4, bcd_to_7seg_3_f5, bcd_to_7seg_3_f6,
       bcd_to_7seg_3_f7;

  bcd_to_7seg bcd_to_7seg_1 (
    .F1(bcd_to_7seg_1_f1), .F2(bcd_to_7seg_1_f2), .F3(bcd_to_7seg_1_f3), .F4(bcd_to_7seg_1_f4),
    .F5(bcd_to_7seg_1_f5), .F6(bcd_to_7seg_1_f6), .F7(bcd_to_7seg_1_f7), .C(A1), .D(A0), .A(1'b0), .B(1'b0));
  _7_Segment_Display u_7_segment_display_1 (
    .g(bcd_to_7seg_1_f1), .f(bcd_to_7seg_1_f2), .a(bcd_to_7seg_1_f3), .b(bcd_to_7seg_1_f4),
    .e(bcd_to_7seg_1_f5), .d(bcd_to_7seg_1_f6), .c(bcd_to_7seg_1_f7));  // open: dp
  bcd_to_7seg bcd_to_7seg_2 (
    .F1(bcd_to_7seg_2_f1), .F2(bcd_to_7seg_2_f2), .F3(bcd_to_7seg_2_f3), .F4(bcd_to_7seg_2_f4),
    .F5(bcd_to_7seg_2_f5), .F6(bcd_to_7seg_2_f6), .F7(bcd_to_7seg_2_f7), .C(B1), .D(B0), .A(1'b0), .B(1'b0));
  _7_Segment_Display u_7_segment_display_2 (
    .g(bcd_to_7seg_2_f1), .f(bcd_to_7seg_2_f2), .a(bcd_to_7seg_2_f3), .b(bcd_to_7seg_2_f4),
    .e(bcd_to_7seg_2_f5), .d(bcd_to_7seg_2_f6), .c(bcd_to_7seg_2_f7));  // open: dp
  two_bit_multiplier two_bit_multiplier_1 (.C3(C3), .C2(C2), .C1(C1), .C0(C0), .A0(A0), .B1(B1), .B0(B0), .A1(A1));
  bcd_to_7seg bcd_to_7seg_3 (
    .F1(bcd_to_7seg_3_f1), .F2(bcd_to_7seg_3_f2), .F3(bcd_to_7seg_3_f3), .F4(bcd_to_7seg_3_f4),
    .F5(bcd_to_7seg_3_f5), .F6(bcd_to_7seg_3_f6), .F7(bcd_to_7seg_3_f7), .C(C1), .D(C0), .A(C3), .B(C2));
  _7_Segment_Display u_7_segment_display_3 (
    .g(bcd_to_7seg_3_f1), .f(bcd_to_7seg_3_f2), .a(bcd_to_7seg_3_f3), .b(bcd_to_7seg_3_f4),
    .e(bcd_to_7seg_3_f5), .d(bcd_to_7seg_3_f6), .c(bcd_to_7seg_3_f7));  // open: dp
endmodule
