// Logisim project 9.circ as structural Verilog
module one_bit_full_adder (
  input  Cin,
  input  A,
  input  B,
  output Cout,
  output F
);

  wire nand_1_out, nand_2_out, nand_3_out, not_1_out, not_2_out;

  not not_1 (not_1_out, Cin);
  not not_2 (not_2_out, A);
  nand nand_1 (nand_1_out, not_1_out, not_2_out);
  nand nand_2 (nand_2_out, Cin, A);
  xor xor_1 (F, Cin, A, B);
  nand nand_3 (nand_3_out, B, nand_1_out);
  nand nand_4 (Cout, nand_3_out, nand_2_out);
endmodule

module four_bit_full_adder (
  input  Cin,
  input  A3,
  input  B3,
  input  A2,
  input  B2,
  input  A1,
  input  B1,
  input  A0,
  input  B0,
  output F3,
  output F2,
  output F1,
  output F0,
  output Cout
);

  wire one_bit_full_adder_2_cout, one_bit_full_adder_3_cout, one_bit_full_adder_4_cout;

  one_bit_full_adder one_bit_full_adder_1 (.Cout(Cout), .F(F3), .A(A3), .B(B3), .Cin(one_bit_full_adder_2_cout));
  one_bit_full_adder one_bit_full_adder_2 (
    .Cout(one_bit_full_adder_2_cout), .F(F2), .A(A2), .B(B2), .Cin(one_bit_full_adder_3_cout));
  one_bit_full_adder one_bit_full_adder_3 (
    .Cout(one_bit_full_adder_3_cout), .F(F1), .A(A1), .B(B1), .Cin(one_bit_full_adder_4_cout));
  one_bit_full_adder one_bit_full_adder_4 (.Cout(one_bit_full_adder_4_cout), .F(F0), .A(A0), .B(B0), .Cin(Cin));
endmodule

module one_bit_full_subractor (
  input  Bin,
  input  A,
  input  B,
  output Bout,
  output F
);

  wire nand_1_out, nand_2_out, nand_3_out, not_1_out, not_2_out, not_3_out;

  not not_1 (not_1_out, Bin);
  not not_2 (not_2_out, A);
  not not_3 (not_3_out, B);
  nand nand_1 (nand_1_out, not_1_out, not_3_out);
  nand nand_2 (nand_2_out, Bin, B);
  ExactlyOne xor_1 (.out(F), .in0(Bin), .in1(A), .in2(B));
  nand nand_3 (nand_3_out, not_2_out, nand_1_out);
  nand nand_4 (Bout, nand_3_out, nand_2_out);
endmodule

module four_bit_full_subtractor (
  input  Bin,
  input  A3,
  input  B3,
  input  A2,
  input  B2,
  input  A1,
  input  B1,
  input  A0,
  input  B0,
  output F3,
  output F2,
  output F1,
  output F0,
  output Bout
);

  wire one_bit_full_subractor_2_bout, one_bit_full_subractor_3_bout, one_bit_full_subractor_4_bout;

  one_bit_full_subractor one_bit_full_subractor_1 (
    .Bout(Bout), .F(F3), .A(A3), .B(B3), .Bin(one_bit_full_subractor_2_bout));
  one_bit_full_subractor one_bit_full_subractor_2 (
    .Bout(one_bit_full_subractor_2_bout), .F(F2), .A(A2), .B(B2), .Bin(one_bit_full_subractor_3_bout));
  one_bit_full_subractor one_bit_full_subractor_3 (
    .Bout(one_bit_full_subractor_3_bout), .F(F1), .A(A1), .B(B1), .Bin(one_bit_full_subractor_4_bout));
  one_bit_full_subractor one_bit_full_subractor_4 (
    .Bout(one_bit_full_subractor_4_bout), .F(F0), .A(A0), .B(B0), .Bin(Bin));
endmodule

module four_bit_AND (
  input  A3,
  input  B3,
  input  A2,
  input  B2,
  input  A1,
  input  B1,
  input  A0,
  input  B0,
  output F3,
  output F2,
  output F1,
  output F0
);

  and and_1 (F3, A3, B3);
  and and_2 (F2, A2, B2);
  and and_3 (F1, A1, B1);
  and and_4 (F0, A0, B0);
endmodule

module four_bit_OR (
  input  A3,
  input  B3,
  input  A2,
  input  B2,
  input  A1,
  input  B1,
  input  A0,
  input  B0,
  output F3,
  output F2,
  output F1,
  output F0
);

  or or_1 (F3, A3, B3);
  or or_2 (F2, A2, B2);
  or or_3 (F1, A1, B1);
  or or_4 (F0, A0, B0);
endmodule

module four_to_one_mux (
  input  A,
  input  B,
  input  I0,
  input  I1,
  input  I2,
  input  I3,
  output Z
);

  wire nand_1_out, nand_2_out, nand_3_out, nand_4_out, nand_5_out, nand_6_out, nand_7_out, nand_8_out,
       not_1_out, not_2_out;

  not not_1 (not_1_out, A);
  not not_2 (not_2_out, B);
  nand nand_1 (nand_1_out, not_2_out, I0);
  nand nand_2 (nand_2_out, B, I1);
  nand nand_3 (nand_3_out, not_2_out, I2);
  nand nand_4 (nand_4_out, B, I3);
  nand nand_5 (nand_5_out, nand_1_out, nand_2_out);
  nand nand_6 (nand_6_out, nand_3_out, nand_4_out);
  nand nand_7 (nand_7_out, not_1_out, nand_5_out);
  nand nand_8 (nand_8_out, A, nand_6_out);
  nand nand_9 (Z, nand_7_out, nand_8_out);
endmodule

module four_bit_alu (
  input  Op1,
  input  Op0,
  input  A3,
  input  A2,
  input  A1,
  input  A0,
  input  B3,
  input  B2,
  input  B1,
  input  B0,
  output C3,
  output C2,
  output C1,
  output C0
);

  wire four_bit_and_1_f0, four_bit_and_1_f1, four_bit_and_1_f2, four_bit_and_1_f3, four_bit_full_adder_1_f0,
       four_bit_full_adder_1_f1, four_bit_full_adder_1_f2, four_bit_full_adder_1_f3,
       four_bit_full_subtractor_1_f0, four_bit_full_subtractor_1_f1, four_bit_full_subtractor_1_f2,
       four_bit_full_subtractor_1_f3, four_bit_or_1_f0, four_bit_or_1_f1, four_bit_or_1_f2, four_bit_or_1_f3;

  four_bit_full_adder four_bit_full_adder_1 (
    .F3(four_bit_full_adder_1_f3), .F2(four_bit_full_adder_1_f2), .F1(four_bit_full_adder_1_f1),
    .F0(four_bit_full_adder_1_f0), .A3(A3), .B3(B3), .A2(A2), .B2(B2), .A1(A1), .B1(B1), .A0(A0), .B0(B0));  // open: Cout, Cin
  four_bit_full_subtractor four_bit_full_subtractor_1 (
    .F3(four_bit_full_subtractor_1_f3), .F2(four_bit_full_subtractor_1_f2),
    .F1(four_bit_full_subtractor_1_f1), .F0(four_bit_full_subtractor_1_f0), .A3(A3), .B3(B3), .A2(A2),
    .B2(B2), .A1(A1), .B1(B1), .A0(A0), .B0(B0));  // open: Bout, Bin
  four_bit_AND four_bit_and_1 (
    .F3(four_bit_and_1_f3), .F2(four_bit_and_1_f2), .F1(four_bit_and_1_f1), .F0(four_bit_and_1_f0), .A3(A3),
    .B3(B3), .A2(A2), .B2(B2), .A1(A1), .B1(B1), .A0(A0), .B0(B0));
  four_bit_OR four_bit_or_1 (
    .F3(four_bit_or_1_f3), .F2(four_bit_or_1_f2), .F1(four_bit_or_1_f1), .F0(four_bit_or_1_f0), .A3(A3),
    .B3(B3), .A2(A2), .B2(B2), .A1(A1), .B1(B1), .A0(A0), .B0(B0));
  four_to_one_mux four_to_one_mux_1 (
    .Z(C3), .I0(four_bit_full_adder_1_f3), .I1(four_bit_full_subtractor_1_f3), .I2(four_bit_and_1_f3),
    .I3(four_bit_or_1_f3), .A(Op1), .B(Op0));
  four_to_one_mux four_to_one_mux_2 (
    .Z(C2), .I0(four_bit_full_adder_1_f2), .I1(four_bit_full_subtractor_1_f2), .I2(four_bit_and_1_f2),
    .I3(four_bit_or_1_f2), .A(Op1), .B(Op0));
  four_to_one_mux four_to_one_mux_3 (
    .Z(C1), .I0(four_bit_full_adder_1_f1), .I1(four_bit_full_subtractor_1_f1), .I2(four_bit_and_1_f1),
    .I3(four_bit_or_1_f1), .A(Op1), .B(Op0));
  four_to_one_mux four_to_one_mux_4 (
    .Z(C0), .I0(four_bit_full_adder_1_f0), .I1(four_bit_full_subtractor_1_f0), .I2(four_bit_and_1_f0),
    .I3(four_bit_or_1_f0), .A(Op1), .B(Op0));
endmodule

module hw4_1 (
  input  in_1,
  input  in_2,
  input  in_3,
  input  in_4,
  input  in_5,
  input  in_6,
  input  in_7,
  input  in_8,
  input  in_9,
  input  in_10,
  output out_11,
  output out_12,
  output out_13,
  output out_14
);

  four_bit_alu four_bit_alu_1 (
    .C2(out_12), .C1(out_13), .C0(out_14), .C3(out_11), .Op1(in_1), .Op0(in_2), .A3(in_3), .A2(in_4),
    .A1(in_5), .A0(in_6), .B3(in_7), .B2(in_8), .B1(in_9), .B0(in_10));
endmodule

module four_to_one_mux_using_mux (
  input  I0,
  input  I1,
  input  I2,
  input  I3,
  input  A,
  input  B,
  output Z
);

  wire multiplexer_1_out, multiplexer_2_out;

  Multiplexer multiplexer_1 (.in0(I0), .in1(I1), .out(multiplexer_1_out), .sel(B));
  Multiplexer multiplexer_2 (.in0(I2), .in1(I3), .out(multiplexer_2_out), .sel(B));
  Multiplexer multiplexer_3 (.in0(multiplexer_1_out), .in1(multiplexer_2_out), .out(Z), .sel(A));
endmodule

module eight_to_one_mux_using_mux1 (
  input  I0,
  input  I1,
  input  I2,
  input  I3,
  input  I4,
  input  I5,
  input  I6,
  input  I7,
  input  A,
  input  B,
  input  C,
  output Z
);

  wire multiplexer_1_out, multiplexer_2_out, multiplexer_3_out, multiplexer_4_out;

  Multiplexer multiplexer_1 (.in0(I0), .in1(I1), .out(multiplexer_1_out), .sel(C));
  Multiplexer multiplexer_2 (.in0(I2), .in1(I3), .out(multiplexer_2_out), .sel(C));
  Multiplexer multiplexer_3 (.in0(I4), .in1(I5), .out(multiplexer_3_out), .sel(C));
  Multiplexer multiplexer_4 (.in0(I6), .in1(I7), .out(multiplexer_4_out), .sel(C));
  four_to_one_mux_using_mux four_to_one_mux_using_mux_1 (
    .Z(Z), .I0(multiplexer_1_out), .I1(multiplexer_2_out), .I2(multiplexer_3_out), .I3(multiplexer_4_out),
    .A(A), .B(B));
endmodule

module eight_to_one_mux_using_mux2 (
  input  I0,
  input  I1,
  input  I2,
  input  I3,
  input  I4,
  input  I5,
  input  I6,
  input  I7,
  input  A,
  input  B,
  input  C,
  output Z
);

  wire four_to_one_mux_using_mux_1_z, four_to_one_mux_using_mux_2_z;

  four_to_one_mux_using_mux four_to_one_mux_using_mux_1 (
    .Z(four_to_one_mux_using_mux_1_z), .I0(I0), .I1(I1), .I2(I2), .I3(I3), .A(B), .B(C));
  four_to_one_mux_using_mux four_to_one_mux_using_mux_2 (
    .Z(four_to_one_mux_using_mux_2_z), .I0(I4), .I1(I5), .I2(I6), .I3(I7), .A(B), .B(C));
  Multiplexer multiplexer_1 (
    .in0(four_to_one_mux_using_mux_1_z), .in1(four_to_one_mux_using_mux_2_z), .out(Z), .sel(A));
endmodule

module mux_ex1_1 (
  input  C,
  input  D,
  input  A,
  input  B,
  output F
);

  wire not_1_out, not_2_out, or_1_out;

  not not_1 (not_1_out, D);
  not not_2 (not_2_out, C);
  or or_1 (or_1_out, not_2_out, not_1_out);
  four_to_one_mux_using_mux four_to_one_mux_using_mux_1 (
    .Z(F), .I0(not_2_out), .I1(or_1_out), .I2(not_1_out), .I3(1'b0), .A(A), .B(B));
endmodule

module mux_ex1_2 (
  input  A,
  input  B,
  input  C,
  input  D,
  output F
);

  wire not_1_out, not_2_out, or_1_out, xor_1_out;

  not not_1 (not_1_out, A);
  not not_2 (not_2_out, B);
  or or_1 (or_1_out, not_1_out, not_2_out);
  xor xor_1 (xor_1_out, A, B);
  four_to_one_mux_using_mux four_to_one_mux_using_mux_1 (
    .Z(F), .I0(or_1_out), .I1(not_1_out), .I2(xor_1_out), .I3(1'b0), .A(C), .B(D));
endmodule

module mux_buff (
  input  I0,
  input  I1,
  input  A,
  output F
);

  wire not_1_out;

  assign F = not_1_out ? I0 : 1'bz;  // Controlled_Buffer controlled_buffer_1
  not not_1 (not_1_out, A);
  assign F = A ? I1 : 1'bz;  // Controlled_Buffer controlled_buffer_2
endmodule

module mux (
  input  I0,
  input  I1,
  input  A,
  output F
);

  Multiplexer multiplexer_1 (.in0(I0), .in1(I1), .out(F), .sel(A));
endmodule

module three_state_buff_switch (
  input  A,
  output C
);

  wire buffer_1_out;

  buf buffer_1 (buffer_1_out, A);
  // Switch B: pin names not known; wires that end beside it: buffer_1_out, C
endmodule

module three_state_buff (
  input  A,
  input  B,
  output C
);

  assign C = B ? A : 1'bz;  // Controlled_Buffer controlled_buffer_1
endmodule

module connecte_three_state_buffer (
  input  A,
  input  B,
  input  C,
  input  D,
  output S1,
  output F,
  output S2
);

  assign F = B ? A : 1'bz;  // Controlled_Buffer controlled_buffer_1
  assign F = D ? C : 1'bz;  // Controlled_Buffer controlled_buffer_2

  assign S1 = F;
  assign S2 = F;
endmodule
