// Logisim project 5.circ as structural Verilog
module circuit_5_6_1 (
  input  a,
  input  b,
  input  c,
  input  d,
  output F
);

  wire and_1_out, and_2_out, and_3_out, not_1_out, not_2_out, not_3_out;

  not not_1 (not_1_out, a);
  not not_2 (not_2_out, b);
  not not_3 (not_3_out, c);
  and and_1 (and_1_out, not_1_out, not_2_out, not_3_out);
  and and_2 (and_2_out, not_1_out, not_2_out, d);
  or or_1 (F, and_1_out, and_2_out, and_3_out);
  and and_3 (and_3_out, a, c, d);
endmodule

module circuit_5_6_2 (
  input  a,
  input  b,
  input  c,
  input  d,
  output F
);

  wire and_1_out, and_2_out, not_1_out, not_2_out, not_3_out, or_1_out;

  not not_1 (not_1_out, a);
  not not_2 (not_2_out, b);
  not not_3 (not_3_out, c);
  or or_1 (or_1_out, not_3_out, d);
  and and_1 (and_1_out, or_1_out, not_1_out, not_2_out);
  and and_2 (and_2_out, a, c, d);
  or or_2 (F, and_1_out, and_2_out);
endmodule
