// Logisim project 7.circ as structural Verilog
module main (
  input  A,
  input  B,
  input  C,
  input  D,
  input  E,
  input  F,
  input  G,
  input  H,
  output Z
);

  wire and_1_out, and_2_out, and_3_out, and_4_out, or_1_out;

  or or_1 (or_1_out, D, E);
  and and_1 (and_1_out, or_1_out, A);
  and and_2 (and_2_out, or_1_out, C);
  and and_3 (and_3_out, A, B, F, G);
  and and_4 (and_4_out, C, F, G);
  or or_2 (Z, and_1_out, and_2_out, and_3_out, and_4_out, H);
endmodule

module citcuit2_1 (
  input  a,
  input  b,
  input  c,
  input  d,
  output F
);

  wire and_1_out, and_2_out, and_3_out, and_4_out, not_1_out, not_2_out, not_3_out;

  not not_1 (not_1_out, a);
  not not_2 (not_2_out, c);
  not not_3 (not_3_out, d);
  and and_1 (and_1_out, not_1_out, not_2_out, d);
  and and_2 (and_2_out, b, not_2_out, d);
  and and_3 (and_3_out, b, c, not_3_out);
  and and_4 (and_4_out, a, c, not_3_out);
  or or_1 (F, and_1_out, and_2_out, and_3_out, and_4_out);
endmodule

module circuit2_2 (
  input  a,
  input  b,
  input  c,
  input  d,
  output F
);

  wire and_1_out, and_2_out, not_1_out, not_2_out, not_3_out, or_1_out, or_2_out;

  not not_1 (not_1_out, a);
  not not_2 (not_2_out, c);
  not not_3 (not_3_out, d);
  or or_1 (or_1_out, not_1_out, b);
  or or_2 (or_2_out, a, b);
  and and_1 (and_1_out, or_1_out, not_2_out, d);
  and and_2 (and_2_out, or_2_out, c, not_3_out);
  or or_3 (F, and_1_out, and_2_out);
endmodule

module circuit2_3 (
  input  a,
  input  b,
  input  c,
  input  d,
  output F
);

  wire not_1_out, not_2_out, not_3_out, or_1_out, or_2_out, or_3_out, or_4_out;

  not not_1 (not_1_out, a);
  not not_2 (not_2_out, c);
  not not_3 (not_3_out, d);
  or or_1 (or_1_out, c, d);
  or or_2 (or_2_out, not_1_out, b, c);
  or or_3 (or_3_out, not_2_out, not_3_out);
  or or_4 (or_4_out, a, b, not_2_out);
  and and_1 (F, or_1_out, or_2_out, or_3_out, or_4_out);
endmodule

module circuit2_4 (
  input  a,
  input  b,
  input  c,
  input  d,
  output F
);

  wire and_1_out, and_2_out, and_3_out, and_4_out, not_1_out, not_2_out, not_3_out, or_1_out, or_2_out;

  not not_1 (not_1_out, a);
  not not_2 (not_2_out, c);
  not not_3 (not_3_out, d);
  and and_1 (and_1_out, not_1_out, d);
  and and_2 (and_2_out, b, d);
  and and_3 (and_3_out, a, not_3_out);
  and and_4 (and_4_out, b, not_3_out);
  or or_1 (or_1_out, c, and_1_out, and_2_out);
  or or_2 (or_2_out, not_2_out, and_3_out, and_4_out);
  and and_5 (F, or_1_out, or_2_out);
endmodule

module andnot (
  input  in_1,
  input  in_2,
  input  in_3,
  input  in_4,
  input  in_5,
  input  in_6,
  input  in_7,
  input  in_8,
  input  in_9,
  input  in_10,
  output out_11,
  output out_12,
  output out_13,
  output out_14,
  output out_15
);

  wire and_1_out, and_3_out, nand_2_out, not_1_out, not_2_out;

  not not_1 (not_1_out, in_9);
  not not_2 (not_2_out, in_10);
  and and_1 (and_1_out, in_1, in_2);
  not not_3 (out_11, and_1_out);
  nand nand_1 (out_12, in_3, in_4);
  and and_2 (out_13, in_5, in_6);
  nand nand_2 (nand_2_out, in_7, in_8);
  not not_4 (out_14, nand_2_out);
  and and_3 (and_3_out, not_1_out, not_2_out);
  not not_5 (out_15, and_3_out);
endmodule

module ornot (
  input  in_1,
  input  in_2,
  input  in_3,
  input  in_4,
  input  in_5,
  input  in_6,
  output out_7,
  output out_8,
  output out_9
);

  wire not_1_out, not_2_out, or_1_out, or_2_out;

  not not_1 (not_1_out, in_5);
  not not_2 (not_2_out, in_6);
  or or_1 (or_1_out, in_1, in_2);
  not not_3 (out_7, or_1_out);
  nor nor_1 (out_8, in_3, in_4);
  or or_2 (or_2_out, not_1_out, not_2_out);
  not not_4 (out_9, or_2_out);
endmodule

module not_nand (
  input  in_1,
  output out_2
);

  nand nand_1 (out_2, in_1, in_1);
endmodule

module and_nand (
  input  in_1,
  input  in_2,
  output out_3
);

  wire nand_1_out;

  nand nand_1 (nand_1_out, in_1, in_2);
  nand nand_2 (out_3, nand_1_out, nand_1_out);
endmodule

module or_of_nand (
  input  in_1,
  input  in_2,
  input  in_3,
  input  in_4,
  input  in_5,
  input  in_6,
  input  in_7,
  input  in_8,
  input  in_9,
  input  in_10,
  output out_11,
  output out_12,
  output out_13,
  output out_14,
  output out_15
);

  wire nand_2_out, nand_3_out, not_1_out, not_2_out, not_3_out, not_4_out;

  nand nand_1 (out_12, in_3, in_4);
  not not_1 (not_1_out, in_5);
  not not_2 (not_2_out, in_6);
  not not_3 (not_3_out, in_7);
  not not_4 (not_4_out, in_8);
  or or_1 (out_15, in_9, in_10);
  nand nand_2 (nand_2_out, in_1, in_1);
  nand nand_3 (nand_3_out, in_2, in_2);
  or or_2 (out_13, not_1_out, not_2_out);
  nand nand_4 (out_14, not_3_out, not_4_out);
  nand nand_5 (out_11, nand_2_out, nand_3_out);
endmodule

module not_nor (
  input  in_1,
  output out_2
);

  nor nor_1 (out_2, in_1, in_1);
endmodule

module or_nor (
  input  in_1,
  input  in_2,
  output out_3
);

  wire nor_1_out;

  nor nor_1 (nor_1_out, in_1, in_2);
  nor nor_2 (out_3, nor_1_out, nor_1_out);
endmodule

module and_nor (
  input  in_1,
  input  in_2,
  input  in_3,
  input  in_4,
  input  in_5,
  input  in_6,
  input  in_7,
  input  in_8,
  input  in_9,
  input  in_10,
  output out_11,
  output out_12,
  output out_13,
  output out_14,
  output out_15
);

  wire nor_1_out, nor_2_out, not_1_out, not_2_out, not_3_out, not_4_out;

  nor nor_1 (nor_1_out, in_1, in_1);
  nor nor_2 (nor_2_out, in_2, in_2);
  nor nor_3 (out_12, in_3, in_4);
  not not_1 (not_1_out, in_5);
  not not_2 (not_2_out, in_6);
  not not_3 (not_3_out, in_7);
  not not_4 (not_4_out, in_8);
  and and_1 (out_15, in_9, in_10);
  nor nor_4 (out_11, nor_1_out, nor_2_out);
  and and_2 (out_13, not_1_out, not_2_out);
  nor nor_5 (out_14, not_3_out, not_4_out);
endmodule

module and_or (
  input  A,
  input  B,
  input  C,
  input  D,
  output F
);

  wire and_1_out, and_2_out, not_1_out, not_2_out;

  not not_1 (not_1_out, B);
  not not_2 (not_2_out, C);
  and and_1 (and_1_out, B, not_2_out);
  and and_2 (and_2_out, not_1_out, C, D);
  or or_1 (F, A, and_1_out, and_2_out);
endmodule

module and_not_not_or (
  input  A,
  input  B,
  input  C,
  input  D,
  output F
);

  wire and_1_out, and_2_out, not_1_out, not_2_out, not_3_out, not_4_out, not_5_out, not_6_out, not_7_out,
       not_8_out;

  not not_1 (not_1_out, B);
  not not_2 (not_2_out, C);
  not not_3 (not_3_out, A);
  and and_1 (and_1_out, B, not_2_out);
  not not_4 (not_4_out, and_1_out);
  and and_2 (and_2_out, not_1_out, C, D);
  not not_5 (not_5_out, and_2_out);
  not not_6 (not_6_out, not_3_out);
  not not_7 (not_7_out, not_4_out);
  not not_8 (not_8_out, not_5_out);
  or or_1 (F, not_6_out, not_7_out, not_8_out);
endmodule

module nand_nand (
  input  A,
  input  B,
  input  C,
  input  D,
  output F
);

  wire nand_1_out, nand_2_out, not_1_out, not_2_out, not_3_out;

  not not_1 (not_1_out, A);
  not not_2 (not_2_out, B);
  not not_3 (not_3_out, C);
  nand nand_1 (nand_1_out, B, not_3_out);
  nand nand_2 (nand_2_out, not_2_out, C, D);
  nand nand_3 (F, not_1_out, nand_1_out, nand_2_out);
endmodule

module not_or_nand (
  input  A,
  input  B,
  input  C,
  input  D,
  output F
);

  wire not_1_out, not_2_out, not_3_out, not_4_out, not_5_out, not_6_out, not_7_out, not_8_out, or_1_out,
       or_2_out;

  not not_1 (not_1_out, A);
  not not_2 (not_2_out, B);
  not not_3 (not_3_out, C);
  not not_4 (not_4_out, B);
  or or_1 (or_1_out, not_4_out, not_5_out);
  not not_5 (not_5_out, not_3_out);
  not not_6 (not_6_out, not_2_out);
  not not_7 (not_7_out, C);
  or or_2 (or_2_out, not_6_out, not_7_out, not_8_out);
  not not_8 (not_8_out, D);
  nand nand_1 (F, not_1_out, or_1_out, or_2_out);
endmodule

module or_nand (
  input  A,
  input  B,
  input  C,
  input  D,
  output F
);

  wire not_1_out, not_2_out, not_3_out, not_4_out, or_1_out, or_2_out;

  not not_1 (not_1_out, A);
  not not_2 (not_2_out, C);
  not not_3 (not_3_out, B);
  not not_4 (not_4_out, D);
  or or_1 (or_1_out, not_3_out, C);
  or or_2 (or_2_out, B, not_2_out, not_4_out);
  nand nand_1 (F, not_1_out, or_1_out, or_2_out);
endmodule

module or_not_not_nand (
  input  A,
  input  B,
  input  C,
  input  D,
  output F
);

  wire not_1_out, not_2_out, not_3_out, not_4_out, not_5_out, not_6_out, not_7_out, not_8_out, not_9_out,
       not_10_out, or_1_out, or_2_out;

  not not_1 (not_1_out, A);
  not not_2 (not_2_out, C);
  not not_3 (not_3_out, B);
  not not_4 (not_4_out, D);
  not not_5 (not_5_out, not_1_out);
  or or_1 (or_1_out, not_3_out, C);
  not not_6 (not_6_out, or_1_out);
  or or_2 (or_2_out, B, not_2_out, not_4_out);
  not not_7 (not_7_out, or_2_out);
  not not_8 (not_8_out, not_5_out);
  not not_9 (not_9_out, not_6_out);
  not not_10 (not_10_out, not_7_out);
  nand nand_1 (F, not_8_out, not_9_out, not_10_out);
endmodule

module nor_or (
  input  A,
  input  B,
  input  C,
  input  D,
  output F
);

  wire nor_1_out, nor_2_out, not_1_out, not_2_out, not_3_out;

  not not_1 (not_1_out, C);
  not not_2 (not_2_out, B);
  not not_3 (not_3_out, D);
  nor nor_1 (nor_1_out, not_2_out, C);
  nor nor_2 (nor_2_out, B, not_1_out, not_3_out);
  or or_1 (F, A, nor_1_out, nor_2_out);
endmodule

module sop_nand_nand (
  input  in_1,
  input  in_2,
  input  in_3,
  input  in_4,
  input  in_5,
  input  in_6,
  input  in_7,
  input  in_8,
  input  in_9,
  input  in_10,
  input  in_11,
  input  in_12,
  output out_13,
  output out_14,
  output out_15
);

  wire and_1_out, and_2_out, and_3_out, and_4_out, nand_1_out, nand_2_out, not_1_out, not_2_out, not_3_out,
       not_4_out;

  and and_1 (and_1_out, in_1, in_2);
  and and_2 (and_2_out, in_3, in_4);
  and and_3 (and_3_out, in_5, in_6);
  not not_1 (not_1_out, and_3_out);
  and and_4 (and_4_out, in_7, in_8);
  not not_2 (not_2_out, and_4_out);
  nand nand_1 (nand_1_out, in_9, in_10);
  nand nand_2 (nand_2_out, in_11, in_12);
  or or_1 (out_13, and_1_out, and_2_out);
  not not_3 (not_3_out, not_1_out);
  not not_4 (not_4_out, not_2_out);
  nand nand_3 (out_15, nand_1_out, nand_2_out);
  or or_2 (out_14, not_3_out, not_4_out);
endmodule

module pos_nor_nor (
  input  in_1,
  input  in_2,
  input  in_3,
  input  in_4,
  input  in_5,
  input  in_6,
  input  in_7,
  input  in_8,
  input  in_9,
  input  in_10,
  input  in_11,
  input  in_12,
  output out_13,
  output out_14,
  output out_15
);

  wire nor_1_out, nor_2_out, not_1_out, not_2_out, not_3_out, not_4_out, or_1_out, or_2_out, or_3_out,
       or_4_out;

  or or_1 (or_1_out, in_1, in_2);
  or or_2 (or_2_out, in_3, in_4);
  or or_3 (or_3_out, in_5, in_6);
  not not_1 (not_1_out, or_3_out);
  or or_4 (or_4_out, in_7, in_8);
  not not_2 (not_2_out, or_4_out);
  nor nor_1 (nor_1_out, in_9, in_10);
  nor nor_2 (nor_2_out, in_11, in_12);
  and and_1 (out_13, or_1_out, or_2_out);
  not not_3 (not_3_out, not_1_out);
  not not_4 (not_4_out, not_2_out);
  nor nor_3 (out_15, nor_1_out, nor_2_out);
  and and_2 (out_14, not_3_out, not_4_out);
endmodule

module multi_level_and_or (
  input  b,
  input  c,
  input  a,
  input  d,
  input  e,
  input  f,
  input  h,
  input  g,
  input  i,
  input  j,
  input  k,
  output out_12
);

  wire and_1_out, and_2_out, and_3_out, and_4_out, not_1_out, not_2_out, not_3_out, not_4_out, not_5_out,
       or_1_out, or_2_out;

  not not_1 (not_1_out, e);
  not not_2 (not_2_out, b);
  or or_1 (or_1_out, d, not_1_out);
  not not_3 (not_3_out, f);
  not not_4 (not_4_out, g);
  and and_1 (and_1_out, not_2_out, c, or_1_out);
  and and_2 (and_2_out, not_3_out, not_4_out);
  or or_2 (or_2_out, and_1_out, and_2_out);
  and and_3 (and_3_out, a, or_2_out);
  not not_5 (not_5_out, i);
  and and_4 (and_4_out, h, not_5_out, j);
  or or_3 (out_12, and_3_out, and_4_out, k);
endmodule

module multi_level_nand (
  input  b,
  input  c,
  input  a,
  input  d,
  input  e,
  input  f,
  input  h,
  input  g,
  input  i,
  input  j,
  input  k,
  output out_12
);

  wire nand_1_out, nand_2_out, nand_3_out, nand_4_out, nand_5_out, nand_6_out, not_1_out, not_2_out,
       not_3_out, not_4_out, not_5_out, not_6_out;

  not not_1 (not_1_out, d);
  not not_2 (not_2_out, b);
  nand nand_1 (nand_1_out, not_1_out, e);
  not not_3 (not_3_out, f);
  not not_4 (not_4_out, g);
  nand nand_2 (nand_2_out, not_2_out, c, nand_1_out);
  nand nand_3 (nand_3_out, not_3_out, not_4_out);
  nand nand_4 (nand_4_out, nand_2_out, nand_3_out);
  nand nand_5 (nand_5_out, a, nand_4_out);
  not not_5 (not_5_out, i);
  nand nand_6 (nand_6_out, h, not_5_out, j);
  not not_6 (not_6_out, k);
  nand nand_7 (out_12, nand_5_out, nand_6_out, not_6_out);
endmodule
