// Logisim project 4.circ as structural Verilog: 8 circuits, main circuit main
module main (
  input  Ci,
  input  in_2,
  input  in_3,
  input  in_4,
  input  in_5,
  output out_6,
  output out_7,
  output C_i_2
);

  wire onebitfulladder_2_cout;

  oneBitFullAdder onebitfulladder_1 (.Cout(C_i_2), .Sum(out_6), .A(in_2), .B(in_3), .Cin(onebitfulladder_2_cout));
  oneBitFullAdder onebitfulladder_2 (.Cout(onebitfulladder_2_cout), .Sum(out_7), .A(in_4), .B(in_5), .Cin(Ci));

  // Notes on the sheet:
  //   S(i+1)
  //   A(i+1)
  //   C(i+1)
  //   B(i+1)
  //   Si
  //   Ai
  //   Bi
endmodule

module N1 (
  input  w,
  input  x,
  input  y,
  input  z,
  output A,
  output B,
  output C
);


  assign A = w;
  assign B = x;
  assign C = y;
endmodule

module N2 (
  input  A,
  input  B,
  input  C,
  output F
);


  assign F = A;
endmodule

module oneBitHalfAdder (
  input  a,
  input  b,
  output x,
  output y
);

  and and_1 (x, a, b);
  xor xor_1 (y, a, b);
endmodule

module twoBitAdder (
  input  A,
  input  B,
  input  C,
  input  D,
  output X,
  output Y,
  output Z
);


  assign X = A;
  assign Y = B;
  assign Z = C;
endmodule

module fourBitAdder (
  input  A3,
  input  A2,
  input  A1,
  input  A0,
  input  B3,
  input  B2,
  input  B1,
  input  B0,
  output S4,
  output S3,
  output S2,
  output S1,
  output S0
);


  assign S0 = B3;
  assign S1 = A0;
  assign S2 = A1;
  assign S3 = A2;
  assign S4 = A3;
endmodule

module oneBitFullAdder (
  input  A,
  input  B,
  input  Cin,
  output Cout,
  output Sum
);

  wire and_1_out, and_2_out, and_3_out, xor_1_out;

  and and_1 (and_1_out, A, B);
  and and_2 (and_2_out, B, Cin);
  and and_3 (and_3_out, Cin, A);
  xor xor_1 (xor_1_out, A, B);
  or or_1 (Cout, and_1_out, and_2_out, and_3_out);
  xor xor_2 (Sum, xor_1_out, Cin);
endmodule

module fourBitFullAdder (
  input  Cin,
  input  A3,
  input  B3,
  input  A2,
  input  B2,
  input  A1,
  input  B1,
  input  A0,
  input  B0,
  output S3,
  output S2,
  output S1,
  output S0,
  output Cout
);

  wire onebitfulladder_2_cout, onebitfulladder_3_cout, onebitfulladder_4_cout;

  oneBitFullAdder onebitfulladder_1 (.Cout(Cout), .Sum(S3), .A(A3), .B(B3), .Cin(onebitfulladder_2_cout));
  oneBitFullAdder onebitfulladder_2 (
    .Cout(onebitfulladder_2_cout), .Sum(S2), .A(A2), .B(B2), .Cin(onebitfulladder_3_cout));
  oneBitFullAdder onebitfulladder_3 (
    .Cout(onebitfulladder_3_cout), .Sum(S1), .A(A1), .B(B1), .Cin(onebitfulladder_4_cout));
  oneBitFullAdder onebitfulladder_4 (.Cout(onebitfulladder_4_cout), .Sum(S0), .A(A0), .B(B0), .Cin(Cin));
endmodule
